# Fritzing sketch robotics (saved by Fritzing 0.9.3b)
breadboards: 1

parts:
  Part1 = Arduino Uno (Rev3) - ICSP
  q4 = Basic Servo [part_number=MG996R]
  q3 = Basic Servo [part_number=MG996R]
  q2 = Basic Servo [part_number=MG996R]
  q1 = Basic Servo [part_number=MG996R]
  VCC1 = Battery block 9V

nets:
  GND: Part1.GND, q4.gnd, q3.gnd, q2.gnd, q1.gnd, VCC1.-
  N1: Part1.D10_PWM/SS, q2.pulse
  N2: Part1.D11_PWM/MOSI, q1.pulse
  N3: Part1.D5_PWM, q4.pulse
  N4: Part1.D6_PWM, q3.pulse
  VCC: Part1.VIN, q4.vcc, q3.vcc, q2.vcc, q1.vcc, VCC1.+
